// Logisim project partial-store.circ as structural Verilog: 1 circuit, main circuit partial_store
module partial_store (
  input  [31:0] Instruction,
  input  [31:0] MemAddress,
  input  [31:0] DataFromReg,
  input  MemWEn,
  output [3:0] MemWriteMask,
  output [31:0] DataToMem
);

  wire and_1_out, comparator_1_eq;
  wire [3:0] multiplexer_4_out, shifter_1_out;
  wire [7:0] byte0;
  wire [15:8] byte1;
  wire [31:0] sb_out, sh_out;
  wire [31:16] byte2;

  Multiplexer #(.select(2), .width(32)) multiplexer_1 (
    .in0({{16{1'b0}}, byte1, byte0}), .in2({byte1, byte0, {16{1'b0}}}), .out(sh_out), .sel(MemAddress[1:0]));  // open: in1, in3
  Multiplexer #(.select(2), .width(32)) multiplexer_2 (
    .in0({{24{1'b0}}, byte0}), .in1({{16{1'b0}}, byte0, {8{1'b0}}}), .in2({{8{1'b0}}, byte0, {16{1'b0}}}),
    .in3({byte0, {24{1'b0}}}), .out(sb_out), .sel(MemAddress[1:0]));
  Multiplexer #(.select(3), .width(32)) multiplexer_3 (
    .in0(sb_out), .in1(sh_out), .in2({byte2, byte1, byte0}), .out(DataToMem), .sel(Instruction[14:12]));  // open: in3, in4, in5, in6, in7
  Multiplexer #(.select(3), .width(4)) multiplexer_4 (
    .in0(4'b0001), .in1(4'b0011), .in2(4'b1111), .out(multiplexer_4_out), .sel(Instruction[14:12]));  // open: in3, in4, in5, in6, in7
  Comparator #(.width(7)) comparator_1 (.a(Instruction[6:0]), .b(7'b0100011), .eq(comparator_1_eq));  // open: gt, lt
  Shifter #(.width(4)) shifter_1 (.in(multiplexer_4_out), .\dist (MemAddress[1:0]), .out(shifter_1_out));
  and and_1 (and_1_out, comparator_1_eq, MemWEn);
  Multiplexer #(.width(4)) multiplexer_5 (.in0(4'b0000), .in1(shifter_1_out), .out(MemWriteMask), .sel(and_1_out));

  // Other names for the same wires on the sheet: OPCode[6:0] = Instruction[6:0]; Fun3[2:0] = Instruction[14:12];
  //   Bottom2[1:0] = MemAddress[1:0]; byte1[7:0] = byte0; byte2[15:0] = {byte1, byte0};
  //   DataFromMem[31:0] = {byte2, byte1, byte0}; sb_byte0[7:0] = byte0; sb_byte1[15:8] = byte0;
  //   sb_byte2[23:16] = byte0; sb_byte3[31:24] = byte0; sh_byte0[15:0] = {byte1, byte0};
  //   sh_byte1[31:16] = {byte1, byte0}; sw_out[31:0] = {byte2, byte1, byte0}

  // Notes on the sheet:
  //   INPUTS to your circuit
  //   sh_out
  //   DON'T CHANGE THE LOCATIONS OF THE INPUTS AND OUTPUTS!
  //   sb_out
  //   sw_out
  //   OUTPUT from your circuit
endmodule
