// Logisim project regfile0.circ as structural Verilog: 1 circuit, main circuit regfile
module regfile (
  input  [4:0] ReadIndex1,
  input  [4:0] ReadIndex2,
  input  [4:0] WriteIndex,
  input  [31:0] WriteData,
  input  RegWEn,
  input  clk,
  output [31:0] ra,
  output [31:0] sp,
  output [31:0] t0,
  output [31:0] t1,
  output [31:0] t2,
  output [31:0] s0,
  output [31:0] s1,
  output [31:0] a0,
  output [31:0] ReadData1,
  output [31:0] ReadData2
);

  wire En1, En2, En4, En5, En7, En8, En9, En15, En16, En17, En18, En19, En20, En21, En22, En23, En24, En25,
       En26, En27, En28, En29, En30, En31, En32;
  wire [4:0] read_reg1;
  wire [31:0] En3, En12, multiplexer_1_out, rd0, rd11, rd12, rd13, rd14, rd15, rd16, rd17, rd18, rd19, rd20,
       rd21, rd22, rd23, rd24, rd25, rd26, rd27, rd28, rd30, rd31, x1, x2, x9, x14, x18, x22, x27, x28, x30,
       x31;

  Demultiplexer #(.select(5)) demultiplexer_1 (
    .out0(En1), .out1(En2), .out2(En3[0]), .out3(En4), .out4(En5), .out5(clk), .out6(En7), .out7(En8),
    .out8(En9), .out9(clk), .out10(clk), .out11(En12[0]), .out12(clk), .out13(clk), .out14(En15),
    .out15(En16), .out16(En17), .out17(En18), .out18(En19), .out19(En20), .out20(En21), .out21(En22),
    .out22(En23), .out23(En24), .out24(En25), .out25(En26), .out26(En27), .out27(En28), .out28(En29),
    .out29(En30), .out30(En31), .out31(En32), .in(RegWEn), .sel(WriteIndex));
  Register #(.width(32)) register_1 (.D({32{1'b0}}), .en(En1), .clk(clk), .Q(rd0));  // open: clr
  Register #(.width(32)) register_2 (
    .D({WriteData[31:1], clk}), .en(En2), .clk(clk), .Q({WriteData[31:1], clk}), .clr(clk));
  Register #(.width(32)) register_3 (.D({WriteData[31:1], clk}), .en(En3[0]), .clk(clk), .Q(sp));  // open: clr
  Register #(.width(32)) register_4 (
    .D({WriteData[31:1], clk}), .en(En4), .clk(clk), .Q({WriteData[31:1], clk}), .clr(clk));
  Register #(.width(32)) register_5 (
    .D({WriteData[31:1], clk}), .en(En5), .clk(clk), .Q({WriteData[31:1], clk}), .clr(clk));
  Register #(.width(32)) register_6 (.D({WriteData[31:1], clk}), .en(clk), .clk(clk), .Q(t0));  // open: clr
  Register #(.width(32)) register_7 (.D({WriteData[31:1], clk}), .en(En7), .clk(clk), .Q(t1));  // open: clr
  Register #(.width(32)) register_8 (.D({WriteData[31:1], clk}), .en(En8), .clk(clk), .Q(t2));  // open: clr
  Register #(.width(32)) register_9 (.D({WriteData[31:1], clk}), .en(En9), .clk(clk), .Q(s0), .clr(x2[0]));
  Register #(.width(32)) register_10 (.D({WriteData[31:1], clk}), .en(clk), .clk(clk), .Q(s1), .clr(x2[0]));
  Register #(.width(32)) register_11 (.D({WriteData[31:1], clk}), .en(clk), .clk(clk), .Q(a0), .clr(clk));
  Register #(.width(32)) register_12 (
    .D({WriteData[31:1], clk}), .en(En12[0]), .clk(clk), .Q({WriteData[31:1], clk}), .clr(clk));
  Register #(.width(32)) register_13 (
    .D({WriteData[31:1], clk}), .en(clk), .clk(clk), .Q({WriteData[31:1], clk}), .clr(clk));
  Register #(.width(32)) register_14 (.D({WriteData[31:1], clk}), .en(clk), .clk(clk), .Q(rd13), .clr(clk));
  Register #(.width(32)) register_15 (.D({WriteData[31:1], clk}), .en(En15), .clk(clk), .Q(rd14));  // open: clr
  Register #(.width(32)) register_16 (.D({WriteData[31:1], clk}), .en(En16), .clk(clk), .Q(rd15));  // open: clr
  Register #(.width(32)) register_17 (.D({WriteData[31:1], clk}), .en(En17), .clk(clk), .Q(rd16));  // open: clr
  Register #(.width(32)) register_18 (.D({WriteData[31:1], clk}), .en(En18), .clk(clk), .Q(rd17));  // open: clr
  Register #(.width(32)) register_19 (.D({WriteData[31:1], clk}), .en(En19), .clk(clk), .Q(rd18));  // open: clr
  Register #(.width(32)) register_20 (.D({WriteData[31:1], clk}), .en(En20), .clk(clk), .Q(rd19));  // open: clr
  Multiplexer #(.select(5), .width(32)) multiplexer_1 (
    .in0(a0), .in1(x1), .in2(x2), .in3({WriteData[31:1], clk}), .in4({WriteData[31:1], clk}),
    .in5({WriteData[31:1], clk}), .in6({WriteData[31:1], clk}), .in7({WriteData[31:1], clk}),
    .in8({WriteData[31:1], clk}), .in9(x9), .in10(sp), .in11(En3), .in12({WriteData[31:1], clk}),
    .in13({WriteData[31:1], clk}), .in14(x14), .in15(En12), .in16({WriteData[31:1], clk}),
    .in17({WriteData[31:1], clk}), .in18(x18), .in19({WriteData[31:1], clk}), .in20({WriteData[31:1], clk}),
    .in21({WriteData[31:1], clk}), .in22(x22), .in23(t0), .in24({WriteData[31:1], clk}),
    .in25({WriteData[31:1], clk}), .in26({WriteData[31:1], clk}), .in27(x27), .in28(x28),
    .in29({WriteData[31:1], clk}), .in30(x30), .in31(x31), .out(multiplexer_1_out), .sel(read_reg1));
  Register #(.width(32)) register_21 (.D({WriteData[31:1], clk}), .en(En21), .clk(clk), .Q(rd20));  // open: clr
  Register #(.width(32)) register_22 (.D({WriteData[31:1], clk}), .en(En22), .clk(clk), .Q(rd21));  // open: clr
  Register #(.width(32)) register_23 (.D({WriteData[31:1], clk}), .en(En23), .clk(clk), .Q(rd22));  // open: clr
  Register #(.width(32)) register_24 (.D({WriteData[31:1], clk}), .en(En24), .clk(clk), .Q(rd23));  // open: clr
  Register #(.width(32)) register_25 (.D({WriteData[31:1], clk}), .en(En25), .clk(clk), .Q(rd24));  // open: clr
  Register #(.width(32)) register_26 (.D({WriteData[31:1], clk}), .en(En26), .clk(clk), .Q(rd25));  // open: clr
  Register #(.width(32)) register_27 (.D({WriteData[31:1], clk}), .en(En27), .clk(clk), .Q(rd26));  // open: clr
  Register #(.width(32)) register_28 (.D({WriteData[31:1], clk}), .en(En28), .clk(clk), .Q(rd27));  // open: clr
  Register #(.width(32)) register_29 (.D({WriteData[31:1], clk}), .en(En29), .clk(clk), .Q(rd28));  // open: clr
  Register #(.width(32)) register_30 (.D({WriteData[31:1], clk}), .en(En30), .clk(clk), .Q(rd28));  // open: clr
  Register #(.width(32)) register_31 (.D({WriteData[31:1], clk}), .en(En31), .clk(clk), .Q(rd30));  // open: clr
  Register #(.width(32)) register_32 (.D({WriteData[31:1], clk}), .en(En32), .clk(clk), .Q(rd31));  // open: clr
  Multiplexer #(.select(5), .width(32)) multiplexer_2 (
    .in0(rd0), .in1({WriteData[31:1], clk}), .in2(sp), .in3({WriteData[31:1], clk}),
    .in4({WriteData[31:1], clk}), .in5(t0), .in6(t1), .in7(t2), .in8(s0), .in9(s1), .in10(a0), .in11(rd11),
    .in12(rd12), .in13(rd13), .in14(rd14), .in15(rd15), .in16(rd16), .in17(rd17), .in18(rd18), .in19(rd19),
    .in20(rd20), .in21(rd21), .in22(rd22), .in23(rd23), .in24(rd24), .in25(rd25), .in26(rd26), .in27(rd27),
    .in28(rd28), .in29(rd28), .in30(rd30), .in31(rd31), .out(ReadData1), .sel(ReadIndex1));
  Multiplexer #(.select(5), .width(32)) multiplexer_3 (
    .in0(rd0), .in1({WriteData[31:1], clk}), .in2(sp), .in3({WriteData[31:1], clk}),
    .in4({WriteData[31:1], clk}), .in5(t0), .in6(t1), .in7(t2), .in8(s0), .in9(s1), .in10(a0), .in11(rd11),
    .in12(rd12), .in13(rd13), .in14(rd14), .in15(rd15), .in16(rd16), .in17(rd17), .in18(rd18), .in19(rd19),
    .in20(rd20), .in21(rd21), .in22(rd22), .in23(rd23), .in24(rd24), .in25(rd25), .in26(rd26), .in27(rd27),
    .in28(rd28), .in29(rd28), .in30(rd30), .in31(rd31), .out(ReadData2), .sel(ReadIndex2));
  // Pins of 1 and 32 bits meet at {WriteData[31:1], clk}
  // Pins of 1 and 32 bits meet at En3
  // Pins of 1 and 32 bits meet at En12
  // Pins of 1 and 32 bits meet at x2

  assign ra = {WriteData[31:1], clk};
  assign WriteData[0] = clk;

  // Other names for the same wires on the sheet: rd29[31:0] = rd28; x0[31:0] = a0;
  //   clk_t[31:0] = {WriteData[31:1], clk}; En6[31:0] = {WriteData[31:1], clk}; En10[31:0] = {WriteData[31:1], clk};
  //   En11[31:0] = {WriteData[31:1], clk}; En13[31:0] = {WriteData[31:1], clk}; En14[31:0] = {WriteData[31:1], clk};
  //   ra11[31:0] = {WriteData[31:1], clk}; ra12[31:0] = {WriteData[31:1], clk}; rd3[31:0] = {WriteData[31:1], clk};
  //   rd4[31:0] = {WriteData[31:1], clk}; x3[31:0] = {WriteData[31:1], clk}; x4[31:0] = {WriteData[31:1], clk};
  //   x5[31:0] = {WriteData[31:1], clk}; x6[31:0] = {WriteData[31:1], clk}; x7[31:0] = {WriteData[31:1], clk};
  //   x8[31:0] = {WriteData[31:1], clk}; x12[31:0] = {WriteData[31:1], clk}; x13[31:0] = {WriteData[31:1], clk};
  //   x16[31:0] = {WriteData[31:1], clk}; x17[31:0] = {WriteData[31:1], clk}; x19[31:0] = {WriteData[31:1], clk};
  //   x20[31:0] = {WriteData[31:1], clk}; x21[31:0] = {WriteData[31:1], clk}; x24[31:0] = {WriteData[31:1], clk};
  //   x25[31:0] = {WriteData[31:1], clk}; x26[31:0] = {WriteData[31:1], clk}; x29[31:0] = {WriteData[31:1], clk};
  //   x10[31:0] = sp; x11[31:0] = En3; x15[31:0] = En12; x23[31:0] = t0

  // Notes on the sheet:
  //   INPUTS to your circuit
  //   DON'T CHANGE THE LOCATIONS OF THE INPUTS AND OUTPUTS!
  //   These are DEBUG/TEST outputs from your circuit.
  //   OUTPUTS from your circuit
endmodule
